# Fritzing sketch Potentiometer (saved by Fritzing 0.9.0b)
breadboards: 3

parts:
  R1 = Rotary Potentiometer (Small) [maximum_resistance=100kΩ package=THT]
  Part1 = Arduino Uno (Rev3)
  LED1 = LED - 5mm [color="Red (633nm)" package="5 mm [THT]"]
  R2 = Resistor [tolerance=±5% resistance=220 package=THT]

nets:
  N1: R1.leg1, Part1.5V
  N2: R1.wiper, Part1.A0
  N3: R1.leg2, Part1.GND, R2.Pin_1
  N4: LED1.cathode, R2.Pin_0
